// Digital circuit bit-slice-chips.dig as structural Verilog
module bit_slice_chips (
  input  clk,
  input  in_2
);

  wire ADDER_OUT, AND_OUT, CARRY_IN, CARRY_OUT, DS0_IN, DS0_OUT, DS1_IN, DS1_OUT, DS2_IN, DS2_OUT, DS3_IN,
       DS3_OUT, LOADREG, MUX0_OUT, MUX1_OUT, MUX_OUT, MUXSEL_A, MUXSEL_B, MUXSEL_C, MUXSEL_D, NAND_OUT,
       NOT_OUT, OR_OUT, REG_IN0, REG_IN1, REG_IN2, REG_IN3, REG_IN4, REG_IN5, REG_IN6, REG_IN7, REG_OUT5,
       REG_OUT6, REG_OUT7, RESET, STACKDIRSEL, XOR_OUT;
  wire [1:0] dipswitch_1_out, eeprom_1_d;

  DipSwitch dipswitch_1 (.out(dipswitch_1_out[0]));
  DipSwitch dipswitch_2 (.out(dipswitch_1_out[1]));
  DipSwitch dipswitch_3 (.out(REG_IN7));
  DipSwitch dipswitch_4 (.out(REG_IN6));
  DipSwitch dipswitch_5 (.out(REG_IN5));
  Button #(.activeLow("true")) LOAD_IR (.out(LOADREG));
  DipSwitch u_MUXSEL_D (.out(REG_IN3));
  DipSwitch STACK_UP_DOWN (.out(REG_IN4));
  EEPROM #(.Bits(2)) eeprom_1 (.A(dipswitch_1_out), .CS(1'b1), .WE(1'b0), .OE(1'b1), .D(eeprom_1_d));
  DipSwitch u_MUXSEL_C (.out(REG_IN2));
  DipSwitch u_MUXSEL_B (.out(REG_IN1));
  DipSwitch u_MUXSEL_A (.out(REG_IN0));
  LED led_1 (.in(eeprom_1_d[0]));
  LED led_2 (.in(eeprom_1_d[1]));
  Button #(.activeLow("true")) u_RESET (.out(RESET));
  PullDown pulldown_1 (.out(CARRY_IN));
  LED led_3 (.in(DS0_OUT));
  LED led_4 (.in(DS1_OUT));
  LED led_5 (.in(DS2_OUT));
  LED led_6 (.in(DS3_OUT));
  Add add_1 (.a(DS0_OUT), .b(DS1_OUT), .c_i(CARRY_IN), .s(ADDER_OUT), .c_o(CARRY_OUT));
  _7408 AND_gate (
    .pin1(DS0_OUT), .pin2(DS1_OUT), .pin3(AND_OUT), .pin4(1'b0), .pin5(1'b0), .pin7(1'b0), .pin9(1'b0),
    .pin10(1'b0), .pin12(1'b0), .pin13(1'b0), .pin14(1'b1));  // open: pin6, pin8, pin11
  PullUp pullup_1 (.out(RESET));
  _74273 _8_bit_register (
    .pin1(RESET), .pin2(MUXSEL_A), .pin3(REG_IN0), .pin4(REG_IN1), .pin5(MUXSEL_B), .pin6(MUXSEL_C),
    .pin7(REG_IN2), .pin8(REG_IN3), .pin9(MUXSEL_D), .pin10(1'b0), .pin11(LOADREG), .pin12(STACKDIRSEL),
    .pin13(REG_IN4), .pin14(REG_IN5), .pin15(REG_OUT5), .pin16(REG_OUT6), .pin17(REG_IN6), .pin18(REG_IN7),
    .pin19(REG_OUT7), .pin20(1'b1));
  _7400 NAND_gate (
    .pin1(DS0_OUT), .pin2(DS1_OUT), .pin3(NAND_OUT), .pin4(1'b0), .pin5(1'b0), .pin7(1'b0), .pin9(1'b0),
    .pin10(1'b0), .pin12(1'b0), .pin13(1'b0), .pin14(1'b1));  // open: pin6, pin8, pin11
  _7432 OR_gate (
    .pin1(DS0_OUT), .pin2(DS1_OUT), .pin3(OR_OUT), .pin4(1'b0), .pin5(1'b0), .pin7(1'b0), .pin9(1'b0),
    .pin10(1'b0), .pin12(1'b0), .pin13(1'b0), .pin14(1'b1));  // open: pin6, pin8, pin11
  _74151 multiplexer0 (
    .pin1(DS3_OUT), .pin2(DS2_OUT), .pin3(DS1_OUT), .pin4(DS0_OUT), .pin5(MUX0_OUT), .pin7(1'b0),
    .pin8(1'b0), .pin9(MUXSEL_C), .pin10(MUXSEL_B), .pin11(MUXSEL_A), .pin12(in_2), .pin13(NAND_OUT),
    .pin14(ADDER_OUT), .pin15(DS0_OUT), .pin16(1'b1));  // open: pin6
  _74151 multiplexer1 (
    .pin1(XOR_OUT), .pin2(OR_OUT), .pin3(AND_OUT), .pin4(NOT_OUT), .pin5(MUX1_OUT), .pin7(1'b0), .pin8(1'b0),
    .pin9(MUXSEL_C), .pin10(MUXSEL_B), .pin11(MUXSEL_A), .pin12(1'b0), .pin13(DS0_OUT), .pin14(DS0_OUT),
    .pin15(DS0_OUT), .pin16(1'b1));  // open: pin6
  _7486 XOR_gate (
    .pin1(DS0_OUT), .pin2(DS1_OUT), .pin3(XOR_OUT), .pin4(1'b0), .pin5(1'b0), .pin7(1'b0), .pin9(1'b0),
    .pin10(1'b0), .pin12(1'b0), .pin13(1'b0), .pin14(1'b1));  // open: pin6, pin8, pin11
  _74157 multiplexer_select (
    .pin1(MUXSEL_D), .pin2(MUX0_OUT), .pin3(MUX1_OUT), .pin4(MUX_OUT), .pin5(1'b0), .pin6(1'b0), .pin8(1'b0),
    .pin10(1'b0), .pin11(1'b0), .pin13(1'b0), .pin14(1'b0), .pin15(1'b0), .pin16(1'b1));  // open: pin7, pin9, pin12
  _7404 NOT_gate (
    .pin1(DS0_OUT), .pin2(NOT_OUT), .pin3(1'b0), .pin5(1'b0), .pin7(1'b0), .pin9(1'b0), .pin11(1'b0),
    .pin13(1'b0), .pin14(1'b1));  // open: pin4, pin6, pin8, pin10, pin12
  _7474 _1_bit_stack_registers (
    .pin1(RESET), .pin2(DS0_IN), .pin3(clk), .pin4(1'b1), .pin5(DS0_OUT), .pin7(1'b0), .pin9(DS1_OUT),
    .pin10(1'b1), .pin11(clk), .pin12(DS1_IN), .pin13(RESET), .pin14(1'b1));  // open: pin6, pin8
  _7474 _1_bit_stack_registers_2 (
    .pin1(RESET), .pin2(DS2_IN), .pin3(clk), .pin4(1'b1), .pin5(DS2_OUT), .pin7(1'b0), .pin9(DS3_OUT),
    .pin10(1'b1), .pin11(clk), .pin12(DS3_IN), .pin13(RESET), .pin14(1'b1));  // open: pin6, pin8
  _74157 stack_direction_input_select (
    .pin1(STACKDIRSEL), .pin2(MUX_OUT), .pin3(DS1_OUT), .pin4(DS0_IN), .pin5(DS0_OUT), .pin6(DS2_OUT),
    .pin7(DS1_IN), .pin8(1'b0), .pin9(DS2_IN), .pin10(DS3_OUT), .pin11(DS1_OUT), .pin12(DS3_IN),
    .pin13(1'b0), .pin14(DS2_OUT), .pin15(1'b0), .pin16(1'b1));

  // Other names for the same wires on the sheet: CLK_DS0 = clk; CLK_DS1 = clk; CLK_DS2 = clk; CLK_DS3 = clk;
  //   DATABUS = in_2; LEFTBIT_0 = DS0_OUT; LEFTBIT_LSB = DS0_OUT; RIGHTBIT_0 = DS0_OUT; RIGHTBIT_MSB = DS0_OUT

  // Notes on the sheet:
  //   contents of eeprom_1 (hex, n*v repeats v):
  //   0,1,a,3
  //   Clock
  //   Logic
  //   Instruction Register
  //   Connected due to 1-bit
  //   Plexing
  //   Data Stack
endmodule
